# Fritzing sketch GATEWAY (saved by Fritzing 0.9.3b)

parts:
  U1 = ESP32-38PinWide [part_number=ESP32-38PinWide]
  SD_card_module1 = SD Card Module

nets:
  N1: U1.VIN, SD_card_module1.+5
  N2: U1.GPIO5, SD_card_module1.CS
  N3: U1.GPIO18, SD_card_module1.SCK
  N4: U1.GPIO19, SD_card_module1.MISO
  N5: U1.GPIO23, SD_card_module1.MOSI
  GND: U1.GND, SD_card_module1.GND

custom parts:
  ESP32-38PinWide: Generic 38-Pin ESP32 with wide format (only access to one side of pins on a breadboard) based on Stephen Lilley's HiLetgo ESP-WROOM-32 ESP32 ESP-32S Development Board.
  SD Card Module: SD Card Module Slot Socket Reader For Arduino ARM MCU
